# Fritzing sketch ar04_4led (saved by Fritzing 0.9.3b)
breadboards: 1

parts:
  부품1 = Arduino Uno (Rev3)
  R1 = Resistor [tolerance=±5% resistance=220 package=THT]
  R2 = Resistor [tolerance=±5% resistance=220 package=THT]
  LED1 = LED - 5mm [color="Green (570nm)" package="5 mm [THT]"]
  LED2 = LED - 5mm [color="Red (633nm)" package="5 mm [THT]"]
  LED3 = LED - 5mm [color="Blue (525nm)" package="5 mm [THT]"]  # not connected
  LED4 = smd LED [color="Yellow (595nm)" package="0603 [SMD]"]
  R3 = Resistor [tolerance=±5% resistance=220 package=THT]
  R4 = Resistor [tolerance=±5% resistance=220 package=THT]

nets:
  N1: 부품1.D9_PWM, LED4.anode
  N2: 부품1.D3_PWM, LED2.anode
  N3: 부품1.D5_PWM, LED1.anode
  N4: 부품1.GND, R1.Pin_1, R2.Pin_1, R3.Pin_1, R4.Pin_1
  N5: R1.Pin_0, LED1.cathode
  N6: R2.Pin_0, LED2.cathode
  N7: LED4.cathode, R3.Pin_0
